# Fritzing sketch CowPi-mk1d-nano-i2c-lcd1602 (saved by Fritzing 0.9.9b)
breadboards: 1

parts:
  LCM1602_IIC2 = LCM1602 IIC [part_number="LCM1602 IIC" chip_label="LCM1602 IIC" package="DIP (Dual Inline) [THT]"]
  LCD2 = LCD screen
  S9 = Pushbutton [package="[THT]"]
  Part2 = Arduino Nano (Rev3.0)
  R1 = Resistor [tolerance=±5% power=0.25 resistance=1k package=THT]
  U3 = SN74LS20N [package="DIP14 [THT]"]
  LED2 = LED - 5mm [color="Red (633nm)" current=0.030 package="5 mm [THT]"]
  S10 = Toggle Switch [package=THT]
  S11 = Toggle Switch [package=THT]
  Keypad4x2 = Keypad Membran 4x4
  S12 = Pushbutton [package="[THT]"]

nets:
  VSS: LCM1602_IIC2.VSS, LCD2.VSS
  VDD: LCM1602_IIC2.VDD, LCD2.VDD
  N1: LCM1602_IIC2.V0, LCD2.V0
  N2: LCM1602_IIC2.RS, LCD2.RS
  N3: LCM1602_IIC2.RW, LCD2.R/W
  N4: LCM1602_IIC2.E, LCD2.E
  N5: LCM1602_IIC2.D0, LCD2.DB0
  N6: LCM1602_IIC2.D1, LCD2.DB1
  N7: LCM1602_IIC2.D2, LCD2.DB2
  N8: LCM1602_IIC2.D3, LCD2.DB3
  N9: LCM1602_IIC2.D4, LCD2.DB4
  N10: LCM1602_IIC2.D5, LCD2.DB5
  N11: LCM1602_IIC2.D6, LCD2.DB6
  N12: LCM1602_IIC2.D7, LCD2.DB7
  N13: LCM1602_IIC2.A, LCD2.LED+
  N14: LCM1602_IIC2.K, LCD2.LED-
  GND: LCM1602_IIC2.GND, LCM1602_IIC2.SCL, S9.Pin_1, S9.Pin_2, Part2.GND, Part2.A5, U3.GND, LED2.cathode, S10.COM, S11.COM, S12.Pin_1, S12.Pin_2
  VCC: LCM1602_IIC2.VCC, LCM1602_IIC2.SDA, Part2.5V, Part2.A4, U3.2C, U3.2D, U3.VCC
  N15: S9.Pin_3, S9.Pin_4, Part2.D9, U3.2B
  N16: Part2.D2, U3.2Y
  N17: Part2.D3, U3.1Y
  N18: Part2.D4, Keypad4x2.Pin1
  N19: Part2.D5, Keypad4x2.Pin2
  N20: Part2.D6, Keypad4x2.Pin3
  N21: Part2.D7, Keypad4x2.Pin4
  N22: Part2.D8, U3.2A, S12.Pin_3, S12.Pin_4
  N23: Part2.D10, S10.L1
  N24: Part2.D11/MOSI, S11.L1
  N25: Part2.D12/MISO, R1.Pin_0
  N26: Part2.A3, U3.1D, Keypad4x2.Pin8
  N27: Part2.A2, U3.1C, Keypad4x2.Pin7
  N28: Part2.A1, U3.1B, Keypad4x2.Pin6
  N29: Part2.A0, U3.1A, Keypad4x2.Pin5
  N30: R1.Pin_1, LED2.anode

custom parts:
  LCM1602 IIC: I2C-Module to use a 1602 or 2004 LCD on with the wire.h libory Serial LCD Modul
  Keypad Membran 4x4: Membrane Keypad 4x4 Matrix
