# Fritzing sketch CowPi-mk1b-nano-spi-max7219 (saved by Fritzing 0.9.9b)
breadboards: 1

parts:
  Part1 = Arduino Nano (Rev3.0)
  R1 = Resistor [tolerance=±5% power=0.25 resistance=1k package=THT]
  LED1 = LED - 5mm [color="Red (633nm)" current=0.030 package="5 mm [THT]"]
  U2 = SN74LS20N [package="DIP14 [THT]"]
  Part2 = MAX7219 8x8 LedMatrix Module
  U5 = MAX7219 [package=dil24]  # not connected
  U6 = 7-SEGMENT-4DIGIT [package=7-segment-4digit]  # not connected
  U7 = 7-SEGMENT-4DIGIT [package=7-segment-4digit]  # not connected
  S1 = Toggle Switch [package=THT]
  S2 = Toggle Switch [package=THT]
  Keypad4x1 = Keypad Membran 4x4
  S6 = Momentary Switch 6mm 2pin
  S7 = Pushbutton [package="[THT]"]

nets:
  GND: Part1.GND, LED1.cathode, U2.GND, Part2.GND, S1.L1, S2.L1, S6.2, S7.Pin_1, S7.Pin_2
  N1: Part1.D2, U2.1Y
  N2: Part1.D3, U2.2Y
  N3: Part1.D4, Keypad4x1.Pin1
  N4: Part1.D5, Keypad4x1.Pin2
  N5: Part1.D6, Keypad4x1.Pin3
  N6: Part1.D7, Keypad4x1.Pin4
  N7: Part1.D8, U2.1B, S6.1
  N8: Part1.D9, U2.1A, S7.Pin_3, S7.Pin_4
  N9: Part1.D10, Part2.CS
  N10: Part1.D11/MOSI, Part2.DIN
  N11: Part1.D12/MISO, R1.Pin_0
  VCC: Part1.5V, U2.1C, U2.1D, U2.VCC, Part2.VCC
  N12: Part1.A5, S2.COM
  N13: Part1.A4, S1.COM
  N14: Part1.A3, U2.2A, Keypad4x1.Pin8
  N15: Part1.A2, U2.2B, Keypad4x1.Pin7
  N16: Part1.A1, U2.2C, Keypad4x1.Pin6
  N17: Part1.A0, U2.2D, Keypad4x1.Pin5
  N18: Part1.D13/SCK, Part2.CLK
  N19: R1.Pin_1, LED1.anode

custom parts:
  MAX7219 8x8 LedMatrix Module: Description: MAX7219 8x8 LedMatrix Red Module Dimensions: 32x32mm Documents:
  Keypad Membran 4x4: Membrane Keypad 4x4 Matrix
  Momentary Switch 6mm 2pin: Momentary Switch 6mm 2 pin Button commonly used for reset or general input.
