# Fritzing sketch CowPi-mk1c-nano-spi-max7219 (saved by Fritzing 0.9.9b)
breadboards: 1

parts:
  S9 = Pushbutton [package="[THT]"]
  Part2 = Arduino Nano (Rev3.0)
  R1 = Resistor [tolerance=±5% power=0.25 resistance=1k package=THT]
  U3 = SN74LS20N [package="DIP14 [THT]"]
  LED2 = LED - 5mm [color="Red (633nm)" current=0.030 package="5 mm [THT]"]
  S10 = Toggle Switch [package=THT]
  S11 = Toggle Switch [package=THT]
  Keypad4x2 = Keypad Membran 4x4
  S12 = Pushbutton [package="[THT]"]
  Part3 = MAX7219 8x8 LedMatrix Module
  U8 = MAX7219 [package=dil24]  # not connected
  U9 = 7-SEGMENT-4DIGIT [package=7-segment-4digit]  # not connected
  U10 = 7-SEGMENT-4DIGIT [package=7-segment-4digit]  # not connected

nets:
  GND: S9.Pin_1, S9.Pin_2, Part2.GND, U3.GND, LED2.cathode, S10.COM, S11.COM, S12.Pin_1, S12.Pin_2, Part3.GND
  N1: S9.Pin_3, S9.Pin_4, Part2.D9, U3.2B
  N2: Part2.D2, U3.2Y
  N3: Part2.D3, U3.1Y
  N4: Part2.D4, Keypad4x2.Pin1
  N5: Part2.D5, Keypad4x2.Pin2
  N6: Part2.D6, Keypad4x2.Pin3
  N7: Part2.D7, Keypad4x2.Pin4
  N8: Part2.D8, U3.2A, S12.Pin_3, S12.Pin_4
  N9: Part2.D10, Part3.CS
  N10: Part2.D11/MOSI, Part3.DIN
  N11: Part2.D12/MISO, R1.Pin_0
  VCC: Part2.5V, U3.2C, U3.2D, U3.VCC, Part3.VCC
  N12: Part2.A5, S10.L1
  N13: Part2.A4, S11.L1
  N14: Part2.A3, U3.1D, Keypad4x2.Pin8
  N15: Part2.A2, U3.1C, Keypad4x2.Pin7
  N16: Part2.A1, U3.1B, Keypad4x2.Pin6
  N17: Part2.A0, U3.1A, Keypad4x2.Pin5
  N18: Part2.D13/SCK, Part3.CLK
  N19: R1.Pin_1, LED2.anode

custom parts:
  Keypad Membran 4x4: Membrane Keypad 4x4 Matrix
  MAX7219 8x8 LedMatrix Module: Description: MAX7219 8x8 LedMatrix Red Module Dimensions: 32x32mm Documents:
