# Fritzing sketch CowPi-mk1e-nano-spi-max7219 (saved by Fritzing 1.0.0rc)
breadboards: 1

parts:
  S9 = Pushbutton [package="[THT]"]
  Part2 = Arduino Nano (Rev3.0)
  R1 = Resistor [tolerance=±5% power=0.25 resistance=1k package=THT]
  S10 = Toggle Switch [package=THT]
  S11 = Toggle Switch [package=THT]
  Keypad4x2 = Keypad Membran 4x4
  S12 = Pushbutton [package="[THT]"]
  LED1 = LED - 5mm [color="Red (633nm)" current=0.030A package="5 mm [THT]"]
  Part3 = MAX7219 8x8 LedMatrix Module
  U1 = 7-SEGMENT-4DIGIT [package=7-segment-4digit]  # not connected
  U2 = 7-SEGMENT-4DIGIT [package=7-segment-4digit]  # not connected

nets:
  GND: S9.Pin_1, S9.Pin_2, Part2.GND, S10.COM, S11.COM, S12.Pin_1, S12.Pin_2, LED1.cathode, Part3.GND
  N1: S9.Pin_3, S9.Pin_4, Part2.D9
  N2: Part2.D4, Keypad4x2.Pin1
  N3: Part2.D5, Keypad4x2.Pin2
  N4: Part2.D6, Keypad4x2.Pin3
  N5: Part2.D7, Keypad4x2.Pin4
  N6: Part2.D8, S12.Pin_3, S12.Pin_4
  N7: Part2.D10, Part3.CS
  N8: Part2.D11/MOSI, Part3.DIN
  N9: Part2.D12/MISO, R1.Pin_0
  5V: Part2.5V, Part3.VCC
  N10: Part2.A5, S10.L1
  N11: Part2.A4, S11.L1
  N12: Part2.A3, Keypad4x2.Pin8
  N13: Part2.A2, Keypad4x2.Pin7
  N14: Part2.A1, Keypad4x2.Pin6
  N15: Part2.A0, Keypad4x2.Pin5
  N16: Part2.D13/SCK, Part3.CLK
  N17: R1.Pin_1, LED1.anode

custom parts:
  Keypad Membran 4x4: Membrane Keypad 4x4 Matrix
  MAX7219 8x8 LedMatrix Module: Description: MAX7219 8x8 LedMatrix Red Module Dimensions: 32x32mm Documents:
