# Fritzing sketch CowPi-mk1ef-nano-nowires (saved by Fritzing 1.0.0rc)
breadboards: 1

parts:
  S9 = Pushbutton [package="[THT]"]
  Part2 = Arduino Nano (Rev3.0)
  R1 = Resistor [tolerance=±5% power=0.25 resistance=1k package=THT]
  S10 = Toggle Switch [package=THT]  # not connected
  S11 = Toggle Switch [package=THT]  # not connected
  Keypad4x2 = Keypad Membran 4x4  # not connected
  S12 = Pushbutton [package="[THT]"]
  LED2 = LED - 5mm [color="Red (633nm)" current=0.030A package="5 mm [THT]"]

nets:
  N1: S9.Pin_1, S9.Pin_2
  N2: S9.Pin_3, S9.Pin_4
  N3: Part2.D12/MISO, R1.Pin_0
  N4: R1.Pin_1, LED2.anode
  N5: S12.Pin_1, S12.Pin_2
  N6: S12.Pin_3, S12.Pin_4

custom parts:
  Keypad Membran 4x4: Membrane Keypad 4x4 Matrix
