# Fritzing sketch CowPi-mk1f-nano-i2c-lcd1602 (saved by Fritzing 1.0.0rc)
breadboards: 1

parts:
  S9 = Pushbutton [package="[THT]"]
  Part2 = Arduino Nano (Rev3.0)
  R1 = Resistor [tolerance=±5% power=0.25 resistance=1k package=THT]
  S10 = Toggle Switch [package=THT]
  S11 = Toggle Switch [package=THT]
  Keypad4x2 = Keypad Membran 4x4
  S12 = Pushbutton [package="[THT]"]
  LED1 = LED - 5mm [color="Red (633nm)" current=0.030A package="5 mm [THT]"]
  LCM1602_IIC1 = LCM1602 IIC [part_number="LCM1602 IIC" chip_label="LCM1602 IIC" package="DIP (Dual Inline) [THT]"]
  LCD1 = LCD screen

nets:
  GND: S9.Pin_1, S9.Pin_2, Part2.GND, Part2.A5, S10.COM, S11.COM, S12.Pin_1, S12.Pin_2, LED1.cathode, LCM1602_IIC1.GND, LCM1602_IIC1.SCL
  N1: S9.Pin_3, S9.Pin_4, Part2.D9
  N2: Part2.D4, Keypad4x2.Pin1
  N3: Part2.D5, Keypad4x2.Pin2
  N4: Part2.D6, Keypad4x2.Pin3
  N5: Part2.D7, Keypad4x2.Pin4
  N6: Part2.D8, S12.Pin_3, S12.Pin_4
  N7: Part2.D10, S10.L1
  N8: Part2.D11/MOSI, S11.L1
  N9: Part2.D12/MISO, R1.Pin_0
  5V: Part2.5V, Part2.A4, LCM1602_IIC1.VCC, LCM1602_IIC1.SDA, LCM1602_IIC1.LED_B
  N10: Part2.A3, Keypad4x2.Pin8
  N11: Part2.A2, Keypad4x2.Pin7
  N12: Part2.A1, Keypad4x2.Pin6
  N13: Part2.A0, Keypad4x2.Pin5
  N14: R1.Pin_1, LED1.anode
  VSS: LCM1602_IIC1.VSS, LCD1.VSS
  VDD: LCM1602_IIC1.VDD, LCD1.VDD
  N15: LCM1602_IIC1.V0, LCD1.V0
  N16: LCM1602_IIC1.RS, LCD1.RS
  N17: LCM1602_IIC1.RW, LCD1.R/W
  N18: LCM1602_IIC1.E, LCD1.E
  N19: LCM1602_IIC1.D0, LCD1.DB0
  N20: LCM1602_IIC1.D1, LCD1.DB1
  N21: LCM1602_IIC1.D2, LCD1.DB2
  N22: LCM1602_IIC1.D3, LCD1.DB3
  N23: LCM1602_IIC1.D4, LCD1.DB4
  N24: LCM1602_IIC1.D5, LCD1.DB5
  N25: LCM1602_IIC1.D6, LCD1.DB6
  N26: LCM1602_IIC1.D7, LCD1.DB7
  N27: LCM1602_IIC1.A, LCD1.LED+
  N28: LCM1602_IIC1.K, LCD1.LED-

custom parts:
  Keypad Membran 4x4: Membrane Keypad 4x4 Matrix
  LCM1602 IIC: I2C-Module to use a 1602 or 2004 LCD on with the wire.h libory Serial LCD Modul
